// Digital circuit D-SPI.dig as structural Verilog
module D_SPI (
  input  [7:0] D0__7,
  input  clk,
  input  E,
  input  MISO,
  input  nRD,
  output SPICLK,
  output MOSI
);

  wire _74165_1_pin1, and_1_out, e_4017_1_p4, e_4017_1_p6, nand_1_out, nand_2_out, nand_3_out, not_1_out,
       not_2_out, not_4_out, nRST_out;

  _74299 _74299_1 (
    .pin1(1'b0), .pin2(1'b0), .pin3(nRD), .pin4(D0__7[1]), .pin5(D0__7[3]), .pin6(D0__7[5]), .pin7(D0__7[7]),
    .pin9(1'b1), .pin10(1'b0), .pin11(1'b0), .pin12(SPICLK), .pin13(D0__7[6]), .pin14(D0__7[4]),
    .pin15(D0__7[2]), .pin16(D0__7[0]), .pin18(MISO), .pin19(1'b1), .pin20(1'b1));  // open: pin8, pin17
  Button #(.activeLow("true")) nRST (.out(nRST_out));
  not not_1 (not_1_out, E);
  not not_2 (not_2_out, clk);
  nand nand_1 (nand_1_out, not_1_out, e_4017_1_p6);
  nand nand_2 (nand_2_out, nRST_out, nand_1_out);
  nand nand_3 (nand_3_out, e_4017_1_p4, not_1_out);
  and and_1 (and_1_out, not_4_out, nand_3_out, not_2_out);
  // e_4017 e_4017_1: pin names not known; wires that end beside it: 1'b1, nand_2_out, and_1_out, e_4017_1_p4, 1'b0, e_4017_1_p6, 1'b0
  _74165 _74165_1 (
    .pin1(_74165_1_pin1), .pin2(and_1_out), .pin3(D0__7[4]), .pin4(D0__7[5]), .pin5(D0__7[6]),
    .pin6(D0__7[7]), .pin8(1'b0), .pin9(MOSI), .pin10(1'b0), .pin11(D0__7[0]), .pin12(D0__7[1]),
    .pin13(D0__7[2]), .pin14(D0__7[3]), .pin15(1'b0), .pin16(1'b1));  // open: pin7
  not not_3 (_74165_1_pin1, e_4017_1_p4);
  and and_2 (SPICLK, clk, not_4_out, _74165_1_pin1);
  not not_4 (not_4_out, e_4017_1_p6);

  // Notes on the sheet:
  //   nRD: default 1
endmodule
