// Digital circuit D-SPI2.dig as structural Verilog
module D_SPI2 (
  input  [7:0] D0__7,
  input  CK,
  input  nE,
  input  MISO,
  input  nRD,
  input  nRST,
  output SPICLK,
  output MOSI
);

  wire _74165_1_pin1, _744017_1_pin3, _744017_1_pin11, and_1_out, nand_1_out, nand_2_out, nand_3_out,
       not_1_out, not_3_out;

  _74299 _74299_1 (
    .pin1(1'b0), .pin2(1'b0), .pin3(nRD), .pin4(D0__7[1]), .pin5(D0__7[3]), .pin6(D0__7[5]), .pin7(D0__7[7]),
    .pin9(1'b1), .pin10(1'b0), .pin11(1'b0), .pin12(SPICLK), .pin13(D0__7[6]), .pin14(D0__7[4]),
    .pin15(D0__7[2]), .pin16(D0__7[0]), .pin18(MISO), .pin19(1'b1), .pin20(1'b1));  // open: pin8, pin17
  not not_1 (not_1_out, CK);
  nand nand_1 (nand_1_out, nE, _744017_1_pin11);
  nand nand_2 (nand_2_out, nRST, nand_1_out);
  nand nand_3 (nand_3_out, _744017_1_pin3, nE);
  and and_1 (and_1_out, not_3_out, nand_3_out, not_1_out);
  _744017 _744017_1 (
    .pin3(_744017_1_pin3), .pin8(1'b0), .pin11(_744017_1_pin11), .pin13(1'b0), .pin14(and_1_out),
    .pin15(nand_2_out), .pin16(1'b1));  // open: pin1, pin2, pin4, pin5, pin6, pin7, pin9, pin10, pin12
  _74165 _74165_1 (
    .pin1(_74165_1_pin1), .pin2(and_1_out), .pin3(D0__7[4]), .pin4(D0__7[5]), .pin5(D0__7[6]),
    .pin6(D0__7[7]), .pin8(1'b0), .pin9(MOSI), .pin10(1'b0), .pin11(D0__7[0]), .pin12(D0__7[1]),
    .pin13(D0__7[2]), .pin14(D0__7[3]), .pin15(1'b0), .pin16(1'b1));  // open: pin7
  not not_2 (_74165_1_pin1, _744017_1_pin3);
  and and_2 (SPICLK, CK, not_3_out, _74165_1_pin1);
  not not_3 (not_3_out, _744017_1_pin11);

  // Notes on the sheet:
  //   nE: default 1
  //   nRD: default 1
  //   nRST: default 1
endmodule

/* Test case:
CK D0..7 ~RST ~E ~RD MISO SPICLK MOSI
#Reset
0  0x00  0    1  1   0    0      0
#Send all zeros
0  0x00  1    1  1   0    0      0
1  0x00  1    1  1   0    0      0
1  0x00  1    0  1   0    0      0
0  0x00  1    0  1   0    0      0
1  0x00  1    0  1   0    1      0
0  0x00  1    0  1   0    0      0
1  0x00  1    0  1   0    1      0
0  0x00  1    0  1   0    0      0
1  0x00  1    0  1   0    1      0
0  0x00  1    0  1   0    0      0
1  0x00  1    0  1   0    1      0
0  0x00  1    0  1   0    0      0
1  0x00  1    0  1   0    1      0
0  0x00  1    0  1   0    0      0
1  0x00  1    0  1   0    1      0
0  0x00  1    0  1   0    0      0
1  0x00  1    0  1   0    1      0
0  0x00  1    0  1   0    0      0
1  0x00  1    0  1   0    1      0
0  0x00  1    0  1   0    0      0
1  0x00  1    0  1   0    0      0
0  0x00  1    1  1   0    0      0
#Send some data - 0x83 MSB first: 10000011
0  0x83  1    1  1   0    0      X
0  0x83  1    0  1   0    0      1
1  0x00  1    0  1   0    1      1
0  0x00  1    1  1   0    0      0
1  0x00  1    1  1   0    1      0
0  0x00  1    1  1   0    0      0
1  0x00  1    1  1   0    1      0
0  0x00  1    1  1   0    0      0
1  0x00  1    1  1   0    1      0
0  0x00  1    1  1   0    0      0
1  0x00  1    1  1   0    1      0
0  0x00  1    1  1   0    0      0
1  0x00  1    1  1   0    1      0
0  0x00  1    1  1   0    0      1
1  0x00  1    1  1   0    1      1
0  0x00  1    1  1   0    0      1
1  0x00  1    1  1   0    1      1
0  0x00  1    1  1   0    0      X
1  0x00  1    1  1   0    0      X
0  0x00  1    1  1   0    0      X
*/
