// Digital circuit e-4017.dig as structural Verilog
module e_4017 (
  input  nCE,
  input  CP,
  input  MR,
  input  VCC,
  input  GND,
  output _0,
  output _1,
  output _2,
  output _3,
  output _4,
  output _5,
  output _6,
  output _7,
  output _8,
  output _9,
  output TC
);

  wire and_1_out, and_2_out, d_ff_as_1_nq, d_ff_as_1_q, d_ff_as_2_nq, d_ff_as_2_q, d_ff_as_3_nq, d_ff_as_3_q,
       d_ff_as_4_nq, d_ff_as_4_q, d_ff_as_5_q, or_1_out;

  and and_1 (and_1_out, ~nCE, CP);  // And
  nor nor_1 (_0, d_ff_as_1_q, d_ff_as_5_q);
  D_FF_AS d_ff_as_1 (.Set(1'b0), .D(TC), .C(and_1_out), .Clr(MR), .Q(d_ff_as_1_q), .nQ(d_ff_as_1_nq));
  nor nor_2 (_1, d_ff_as_1_nq, d_ff_as_2_q);
  nor nor_3 (_2, d_ff_as_3_q, d_ff_as_2_nq);
  or or_1 (or_1_out, d_ff_as_3_q, d_ff_as_1_q);
  D_FF_AS d_ff_as_2 (.Set(1'b0), .D(d_ff_as_1_q), .C(and_1_out), .Clr(MR), .Q(d_ff_as_2_q), .nQ(d_ff_as_2_nq));
  nor nor_4 (_3, d_ff_as_3_nq, d_ff_as_4_q);
  nor nor_5 (_4, d_ff_as_4_nq, d_ff_as_5_q);
  and and_2 (and_2_out, or_1_out, d_ff_as_2_q);
  D_FF_AS d_ff_as_3 (.Set(1'b0), .D(and_2_out), .C(and_1_out), .Clr(MR), .Q(d_ff_as_3_q), .nQ(d_ff_as_3_nq));
  nor nor_6 (_5, TC, d_ff_as_1_nq);
  nor nor_7 (_6, d_ff_as_2_nq, d_ff_as_1_q);
  D_FF_AS d_ff_as_4 (.Set(1'b0), .D(d_ff_as_3_q), .C(and_1_out), .Clr(MR), .Q(d_ff_as_4_q), .nQ(d_ff_as_4_nq));
  nor nor_8 (_7, d_ff_as_3_nq, d_ff_as_2_q);
  PowerSupply powersupply_1 (.VDD(VCC), .GND(GND));
  nor nor_9 (_8, d_ff_as_3_q, d_ff_as_4_nq);
  D_FF_AS d_ff_as_5 (.Set(1'b0), .D(d_ff_as_4_q), .C(and_1_out), .Clr(MR), .Q(d_ff_as_5_q), .nQ(TC));
  nor nor_10 (_9, TC, d_ff_as_4_q);

  // Notes on the sheet:
  //   nCE: pin 13
  //   CP: pin 14
  //   MR: pin 15
  //   _0: pin 3
  //   _1: pin 2
  //   _2: pin 4
  //   _3: pin 7
  //   _4: pin 10
  //   _5: pin 1
  //   _6: pin 5
  //   _7: pin 6
  //   _8: pin 9
  //   _9: pin 11
  //   TC: pin 12
  //   VCC: pin 16, default 1
  //   GND: pin 8
endmodule
