// Digital circuit shtest.dig as structural Verilog
module shtest (
  input  S0,
  input  nOE1,
  input  nOE2,
  input  S1,
  input  DS7,
  input  DS0,
  input  CP
);

  wire _74299_1_pin5, _74299_1_pin6, _74299_1_pin7, _74299_1_pin8, _74299_1_pin13, _74299_1_pin14,
       _74299_1_pin15, _74299_1_pin17, and_1_out, driver_1_out, driver_2_out, MR_out, switchdt_1_p2,
       switchdt_2_p1, switchdt_3_p1, switchdt_4_p1, switchdt_5_p1, switchdt_6_p1, switchdt_7_p1,
       switchdt_8_p1;

  Button #(.activeLow("true")) MR (.out(MR_out));
  and and_1 (and_1_out, S1, S0);
  LED led_1 (.in(_74299_1_pin17));
  LED led_2 (.in(driver_1_out));
  LED led_3 (.in(driver_2_out));
  assign driver_1_out = and_1_out ? switchdt_1_p2 : 1'bz;  // Driver driver_1
  assign driver_2_out = and_1_out ? switchdt_2_p1 : 1'bz;  // Driver driver_2
  // SwitchDT switchdt_1: pin names not known; wires that end beside it: 1'b0, switchdt_1_p2, 1'b1, 1'b0
  // SwitchDT switchdt_2: pin names not known; wires that end beside it: switchdt_2_p1, 1'b1, 1'b0
  _74299 _74299_1 (
    .pin1(S0), .pin2(nOE1), .pin3(nOE2), .pin4(driver_2_out), .pin5(_74299_1_pin5), .pin6(_74299_1_pin6),
    .pin7(_74299_1_pin7), .pin8(_74299_1_pin8), .pin9(MR_out), .pin10(1'b0), .pin11(DS0), .pin12(CP),
    .pin13(_74299_1_pin13), .pin14(_74299_1_pin14), .pin15(_74299_1_pin15), .pin16(driver_1_out),
    .pin17(_74299_1_pin17), .pin18(DS7), .pin19(S1), .pin20(1'b1));
  LED led_4 (.in(_74299_1_pin5));
  LED led_5 (.in(_74299_1_pin15));
  assign _74299_1_pin15 = and_1_out ? switchdt_3_p1 : 1'bz;  // Driver driver_3
  assign _74299_1_pin5 = and_1_out ? switchdt_4_p1 : 1'bz;  // Driver driver_4
  // SwitchDT switchdt_3: pin names not known; wires that end beside it: switchdt_3_p1, 1'b1, 1'b0
  // SwitchDT switchdt_4: pin names not known; wires that end beside it: switchdt_4_p1, 1'b1, 1'b0
  LED led_6 (.in(_74299_1_pin14));
  LED led_7 (.in(_74299_1_pin6));
  assign _74299_1_pin14 = and_1_out ? switchdt_5_p1 : 1'bz;  // Driver driver_5
  assign _74299_1_pin6 = and_1_out ? switchdt_6_p1 : 1'bz;  // Driver driver_6
  // SwitchDT switchdt_5: pin names not known; wires that end beside it: switchdt_5_p1, 1'b1, 1'b0
  // SwitchDT switchdt_6: pin names not known; wires that end beside it: switchdt_6_p1, 1'b1, 1'b0
  LED led_8 (.in(_74299_1_pin13));
  LED led_9 (.in(_74299_1_pin7));
  assign _74299_1_pin13 = and_1_out ? switchdt_7_p1 : 1'bz;  // Driver driver_7
  assign _74299_1_pin7 = and_1_out ? switchdt_8_p1 : 1'bz;  // Driver driver_8
  // SwitchDT switchdt_7: pin names not known; wires that end beside it: switchdt_7_p1, 1'b1, 1'b0
  // SwitchDT switchdt_8: pin names not known; wires that end beside it: switchdt_8_p1, 1'b1
  LED led_10 (.in(_74299_1_pin8));
endmodule
