// Logisim project 299.circ as structural Verilog: 2 circuits, main circuit main
module main (
  input  in_1,
  input  in_2,
  input  in_3,
  input  in_4,
  input  in_5,
  input  in_6,
  input  in_7
);

  wire clock_1_out, n299_1_q0, n299_1_q2;

  Clock clock_1 (.out(clock_1_out));
  _299 u_299_1 (
    .OE1B(in_1), .OE2B(in_2), .S0(in_4), .S1(in_5), .CP(clock_1_out), .Q0(n299_1_q0), .IO0(in_3), .IO1(in_6),
    .IO2(in_7), .Q2(n299_1_q2));  // open: DS0, DS7
  LED led_1 (.in(n299_1_q0));
  LED led_2 (.in(in_3));
  LED led_3 (.in(in_6));
  LED led_4 (.in(in_7));
  LED led_5 (.in(n299_1_q2));
endmodule

module _299 (
  input  OE1B,
  input  OE2B,
  input  S0,
  input  DS0,
  input  S1,
  input  CP,
  input  DS7,
  output Q0,
  output IO0,
  output IO1,
  output IO2,
  output Q2
);

  wire and_1_out, d_ff_2_q, multiplexer_1_out, multiplexer_2_out, multiplexer_3_out, nor_1_out;

  and and_1 (and_1_out, S0, S1);
  Multiplexer #(.select(2)) multiplexer_1 (
    .in0(Q0), .in1(DS0), .in2(d_ff_2_q), .in3(IO0), .out(multiplexer_1_out), .sel({S1, S0}), .en(1'b1));
  Multiplexer #(.select(2)) multiplexer_2 (
    .in0(d_ff_2_q), .in1(Q0), .in2(Q2), .in3(IO1), .out(multiplexer_2_out), .sel({S1, S0}), .en(1'b1));
  Multiplexer #(.select(2)) multiplexer_3 (
    .in0(Q2), .in1(d_ff_2_q), .in2(DS7), .in3(IO2), .out(multiplexer_3_out), .sel({S1, S0}), .en(1'b1));
  nor nor_1 (nor_1_out, OE1B, OE2B, and_1_out);
  D_Flip_Flop d_ff_1 (.clk(CP), .D(multiplexer_1_out), .Q(Q0));  // open: Qn, preset, en, reset
  D_Flip_Flop d_ff_2 (.clk(CP), .D(multiplexer_2_out), .Q(d_ff_2_q), .en(1'b1));  // open: Qn, preset, reset
  D_Flip_Flop d_ff_3 (.clk(CP), .D(multiplexer_3_out), .Q(Q2), .en(1'b1));  // open: Qn, preset, reset
  assign IO0 = nor_1_out ? Q0 : 1'bz;  // Controlled_Buffer controlled_buffer_1
  assign IO1 = nor_1_out ? d_ff_2_q : 1'bz;  // Controlled_Buffer controlled_buffer_2
  assign IO2 = nor_1_out ? Q2 : 1'bz;  // Controlled_Buffer controlled_buffer_3
endmodule
