// Logisim project SPI.circ as structural Verilog: 1 circuit, main circuit main
module main (
);

  wire and_1_out, and_2_out, and_3_out, and_4_out, and_5_out, and_6_out, and_7_out, and_8_out, and_9_out,
       and_10_out, and_11_out, and_12_out, and_13_out, and_14_out, and_15_out, and_16_out, and_17_out,
       and_18_out, and_19_out, clock_1_out, d_ff_1_q, d_ff_1_qn, d_ff_2_q, d_ff_3_q, d_ff_4_q, d_ff_5_q,
       d_ff_6_q, d_ff_6_qn, d_ff_7_q, d_ff_8_q, d_ff_9_q, d_ff_9_qn, d_ff_10_q, d_ff_11_q, d_ff_12_q,
       d_ff_12_qn, d_ff_13_q, d_ff_14_q, d_ff_15_q, d_ff_15_qn, d_ff_16_q, d_ff_17_q, d_ff_18_q, d_ff_19_q,
       d_ff_20_q, d_ff_21_q, E_out, MISO_out, nand_1_out, nand_2_out, nand_3_out, nor_1_out, nor_2_out,
       nor_3_out, nor_4_out, nor_5_out, nor_6_out, nor_7_out, nor_8_out, nor_9_out, nor_10_out, not_1_out,
       not_2_out, not_3_out, not_4_out, not_5_out, not_6_out, not_7_out, not_8_out, not_9_out, not_10_out,
       not_11_out, not_12_out, not_13_out, not_14_out, or_1_out, RSTB_out;
  wire [7:0] rom_1_data;

  not not_1 (not_1_out, RSTB_out);
  Button RSTB (.out(RSTB_out));
  not not_2 (not_2_out, E_out);
  Button E (.out(E_out));
  Clock clock_1 (.out(clock_1_out));
  not not_3 (not_3_out, clock_1_out);
  ROM #(.addrWidth(2)) rom_1 (.addr(2'b00), .data(rom_1_data), .sel(1'b1));
  nor nor_1 (nor_1_out, d_ff_15_q, d_ff_1_q);
  not not_4 (not_4_out, nor_1_out);
  nand nand_1 (nand_1_out, not_2_out, nor_1_out);
  and and_1 (and_1_out, not_3_out, nand_1_out, not_11_out);
  not not_5 (not_5_out, not_4_out);
  nand nand_2 (nand_2_out, not_2_out, nor_10_out);
  nand nand_3 (nand_3_out, nand_2_out, not_1_out);
  nor nor_2 (nor_2_out, d_ff_6_q, d_ff_1_qn);
  and and_2 (and_2_out, rom_1_data[0], not_5_out);
  and and_3 (and_3_out, not_6_out, not_5_out);
  not not_6 (not_6_out, and_2_out);
  D_Flip_Flop d_ff_1 (
    .clk(and_1_out), .D(d_ff_15_qn), .Q(d_ff_1_q), .Qn(d_ff_1_qn), .en(1'b1), .reset(nand_3_out));  // open: preset
  nor nor_3 (nor_3_out, d_ff_12_q, d_ff_9_qn);
  nor nor_4 (nor_4_out, d_ff_6_qn, d_ff_9_q);
  and and_4 (and_4_out, rom_1_data[1], not_5_out);
  D_Flip_Flop d_ff_2 (
    .clk(and_1_out), .D(d_ff_3_q), .Q(d_ff_2_q), .preset(and_4_out), .en(1'b1), .reset(and_5_out));  // open: Qn
  D_Flip_Flop d_ff_3 (
    .clk(and_1_out), .D(1'b0), .Q(d_ff_3_q), .preset(and_2_out), .en(1'b1), .reset(and_3_out));  // open: Qn
  and and_5 (and_5_out, not_7_out, not_5_out);
  not not_7 (not_7_out, and_4_out);
  D_Flip_Flop d_ff_4 (.clk(and_16_out), .D(d_ff_5_q), .Q(d_ff_4_q));  // open: Qn, preset, en, reset
  D_Flip_Flop d_ff_5 (.clk(and_16_out), .D(MISO_out), .Q(d_ff_5_q));  // open: Qn, preset, en, reset
  or or_1 (or_1_out, d_ff_9_q, d_ff_1_q);
  D_Flip_Flop d_ff_6 (
    .clk(and_1_out), .D(d_ff_1_q), .Q(d_ff_6_q), .Qn(d_ff_6_qn), .en(1'b1), .reset(nand_3_out));  // open: preset
  nor nor_5 (nor_5_out, d_ff_15_q, d_ff_12_qn);
  and and_6 (and_6_out, rom_1_data[3], not_5_out);
  and and_7 (and_7_out, rom_1_data[2], not_5_out);
  D_Flip_Flop d_ff_7 (
    .clk(and_1_out), .D(d_ff_2_q), .Q(d_ff_7_q), .preset(and_7_out), .en(1'b1), .reset(and_8_out));  // open: Qn
  and and_8 (and_8_out, not_8_out, not_5_out);
  not not_8 (not_8_out, and_7_out);
  D_Flip_Flop d_ff_8 (.clk(and_16_out), .D(d_ff_4_q), .Q(d_ff_8_q));  // open: Qn, preset, en, reset
  and and_9 (and_9_out, or_1_out, d_ff_6_q);
  D_Flip_Flop d_ff_9 (
    .clk(and_1_out), .D(and_9_out), .Q(d_ff_9_q), .Qn(d_ff_9_qn), .en(1'b1), .reset(nand_3_out));  // open: preset
  nor nor_6 (nor_6_out, d_ff_1_q, d_ff_6_qn);
  nor nor_7 (nor_7_out, d_ff_1_qn, d_ff_15_qn);
  and and_10 (and_10_out, rom_1_data[4], not_5_out);
  D_Flip_Flop d_ff_10 (
    .clk(and_1_out), .D(d_ff_7_q), .Q(d_ff_10_q), .preset(and_6_out), .en(1'b1), .reset(and_11_out));  // open: Qn
  and and_11 (and_11_out, not_9_out, not_5_out);
  not not_9 (not_9_out, and_6_out);
  D_Flip_Flop d_ff_11 (.clk(and_16_out), .D(d_ff_8_q), .Q(d_ff_11_q));  // open: Qn, preset, en, reset
  D_Flip_Flop d_ff_12 (
    .clk(and_1_out), .D(d_ff_9_q), .Q(d_ff_12_q), .Qn(d_ff_12_qn), .en(1'b1), .reset(nand_3_out));  // open: preset
  nor nor_8 (nor_8_out, d_ff_6_q, d_ff_9_qn);
  nor nor_9 (nor_9_out, d_ff_12_qn, d_ff_9_q);
  and and_12 (and_12_out, rom_1_data[5], not_5_out);
  D_Flip_Flop d_ff_13 (
    .clk(and_1_out), .D(d_ff_10_q), .Q(d_ff_13_q), .preset(and_10_out), .en(1'b1), .reset(and_13_out));  // open: Qn
  and and_13 (and_13_out, not_10_out, not_5_out);
  not not_10 (not_10_out, and_10_out);
  D_Flip_Flop d_ff_14 (.clk(and_16_out), .D(d_ff_11_q), .Q(d_ff_14_q));  // open: Qn, preset, en, reset
  D_Flip_Flop d_ff_15 (
    .clk(and_1_out), .D(d_ff_12_q), .Q(d_ff_15_q), .Qn(d_ff_15_qn), .en(1'b1), .reset(nand_3_out));  // open: preset
  nor nor_10 (nor_10_out, d_ff_12_q, d_ff_15_qn);
  not not_11 (not_11_out, nor_10_out);
  and and_14 (and_14_out, rom_1_data[6], not_5_out);
  D_Flip_Flop d_ff_16 (
    .clk(and_1_out), .D(d_ff_13_q), .Q(d_ff_16_q), .preset(and_12_out), .en(1'b1), .reset(and_15_out));  // open: Qn
  and and_15 (and_15_out, not_12_out, not_5_out);
  not not_12 (not_12_out, and_12_out);
  not not_13 (not_13_out, and_14_out);
  D_Flip_Flop d_ff_17 (.clk(and_16_out), .D(d_ff_14_q), .Q(d_ff_17_q));  // open: Qn, preset, en, reset
  and and_16 (and_16_out, not_11_out, not_4_out, clock_1_out);
  and and_17 (and_17_out, rom_1_data[7], not_5_out);
  D_Flip_Flop d_ff_18 (
    .clk(and_1_out), .D(d_ff_16_q), .Q(d_ff_18_q), .preset(and_14_out), .en(1'b1), .reset(and_18_out));  // open: Qn
  and and_18 (and_18_out, not_13_out, not_5_out);
  not not_14 (not_14_out, and_17_out);
  D_Flip_Flop d_ff_19 (.clk(and_16_out), .D(d_ff_17_q), .Q(d_ff_19_q));  // open: Qn, preset, en, reset
  LED SPICLK (.in(and_16_out));
  LED MOSI (.in(d_ff_20_q));
  D_Flip_Flop d_ff_20 (
    .clk(and_1_out), .D(d_ff_18_q), .Q(d_ff_20_q), .preset(and_17_out), .en(1'b1), .reset(and_19_out));  // open: Qn
  Button MISO (.out(MISO_out));
  and and_19 (and_19_out, not_14_out, not_5_out);
  D_Flip_Flop d_ff_21 (.clk(and_16_out), .D(d_ff_19_q), .Q(d_ff_21_q));  // open: Qn, preset, en, reset

  // Notes on the sheet:
  //   contents of rom_1 (hex, n*v repeats v):
  //   25
endmodule
