// Logisim project SPI3.circ as structural Verilog: 3 circuits, main circuit main
module main (
);

  wire and_1_out, and_2_out, clock_1_out, d_ff_1_q, d_ff_2_q, d_ff_3_q, d_ff_4_q, d_ff_5_q, d_ff_6_q,
       d_ff_7_q, d_ff_8_q, decade_counter_1__0, decade_counter_1__9, E_out, MISO_out, nand_1_out, nand_2_out,
       nand_3_out, not_1_out, not_2_out, not_3_out, not_4_out, not_5_out, RSTB_out, shift_1_q;
  wire [7:0] rom_1_data;

  Button RSTB (.out(RSTB_out));
  not not_1 (not_1_out, RSTB_out);
  Button E (.out(E_out));
  not not_2 (not_2_out, E_out);
  Clock clock_1 (.out(clock_1_out));
  not not_3 (not_3_out, clock_1_out);
  D_Flip_Flop d_ff_1 (.clk(and_2_out), .D(MISO_out), .Q(d_ff_1_q));  // open: Qn, preset, en, reset
  ROM #(.addrWidth(2)) rom_1 (.addr(2'b00), .data(rom_1_data), .sel(1'b1));
  not not_4 (not_4_out, decade_counter_1__0);
  nand nand_1 (nand_1_out, not_2_out, decade_counter_1__0);
  and and_1 (and_1_out, not_3_out, nand_1_out, not_5_out);
  D_Flip_Flop d_ff_2 (.clk(and_2_out), .D(d_ff_1_q), .Q(d_ff_2_q));  // open: Qn, preset, en, reset
  D_Flip_Flop d_ff_3 (.clk(and_2_out), .D(d_ff_2_q), .Q(d_ff_3_q));  // open: Qn, preset, en, reset
  decade_counter decade_counter_1 (
    .CEB(1'b0), .CP(and_1_out), .MR(nand_2_out), ._0(decade_counter_1__0), ._9(decade_counter_1__9));  // open: _1, _2, _3, _4, _5, _6, _7, _8, TC
  nand nand_2 (nand_2_out, not_1_out, nand_3_out);
  nand nand_3 (nand_3_out, not_2_out, decade_counter_1__9);
  D_Flip_Flop d_ff_4 (.clk(and_2_out), .D(d_ff_3_q), .Q(d_ff_4_q));  // open: Qn, preset, en, reset
  not not_5 (not_5_out, decade_counter_1__9);
  D_Flip_Flop d_ff_5 (.clk(and_2_out), .D(d_ff_4_q), .Q(d_ff_5_q));  // open: Qn, preset, en, reset
  and and_2 (and_2_out, not_5_out, not_4_out, clock_1_out);
  shift shift_1 (
    .CLK_INH(1'b0), .CLK(and_1_out), .SER(1'b0), .Q(shift_1_q), .SH_LDB(not_4_out), .D0__7(rom_1_data));  // open: QB
  D_Flip_Flop d_ff_6 (.clk(and_2_out), .D(d_ff_5_q), .Q(d_ff_6_q));  // open: Qn, preset, en, reset
  D_Flip_Flop d_ff_7 (.clk(and_2_out), .D(d_ff_6_q), .Q(d_ff_7_q));  // open: Qn, preset, en, reset
  LED SPICLK (.in(and_2_out));
  LED MOSI (.in(shift_1_q));
  Button MISO (.out(MISO_out));
  D_Flip_Flop d_ff_8 (.clk(and_2_out), .D(d_ff_7_q), .Q(d_ff_8_q));  // open: Qn, preset, en, reset

  // Notes on the sheet:
  //   contents of rom_1 (hex, n*v repeats v):
  //   25
endmodule

module decade_counter (
  input  CEB,
  input  CP,
  input  MR,
  output _0,
  output _1,
  output _2,
  output _3,
  output _4,
  output _5,
  output _6,
  output _7,
  output _8,
  output _9,
  output TC
);

  wire and_1_out, and_2_out, d_ff_1_q, d_ff_1_qn, d_ff_2_q, d_ff_2_qn, d_ff_3_q, d_ff_3_qn, d_ff_4_q,
       d_ff_4_qn, d_ff_5_q, not_1_out, or_1_out;

  not not_1 (not_1_out, CEB);
  nor nor_1 (_0, d_ff_5_q, d_ff_1_q);
  and and_1 (and_1_out, not_1_out, CP);
  nor nor_2 (_1, d_ff_2_q, d_ff_1_qn);
  D_Flip_Flop d_ff_1 (.clk(and_1_out), .D(TC), .Q(d_ff_1_q), .Qn(d_ff_1_qn), .en(1'b1), .reset(MR));  // open: preset
  nor nor_3 (_2, d_ff_2_qn, d_ff_3_q);
  nor nor_4 (_3, d_ff_4_q, d_ff_3_qn);
  or or_1 (or_1_out, d_ff_3_q, d_ff_1_q);
  D_Flip_Flop d_ff_2 (
    .clk(and_1_out), .D(d_ff_1_q), .Q(d_ff_2_q), .Qn(d_ff_2_qn), .en(1'b1), .reset(MR));  // open: preset
  nor nor_5 (_4, d_ff_5_q, d_ff_4_qn);
  and and_2 (and_2_out, or_1_out, d_ff_2_q);
  D_Flip_Flop d_ff_3 (
    .clk(and_1_out), .D(and_2_out), .Q(d_ff_3_q), .Qn(d_ff_3_qn), .en(1'b1), .reset(MR));  // open: preset
  nor nor_6 (_5, d_ff_1_qn, TC);
  nor nor_7 (_6, d_ff_1_q, d_ff_2_qn);
  D_Flip_Flop d_ff_4 (
    .clk(and_1_out), .D(d_ff_3_q), .Q(d_ff_4_q), .Qn(d_ff_4_qn), .en(1'b1), .reset(MR));  // open: preset
  nor nor_8 (_8, d_ff_4_qn, d_ff_3_q);
  nor nor_9 (_7, d_ff_2_q, d_ff_3_qn);
  D_Flip_Flop d_ff_5 (.clk(and_1_out), .D(d_ff_4_q), .Q(d_ff_5_q), .Qn(TC), .en(1'b1), .reset(MR));  // open: preset
  nor nor_10 (_9, d_ff_4_q, TC);
endmodule

module shift (
  input  SH_LDB,
  input  [7:0] D0__7,
  input  CLK_INH,
  input  CLK,
  input  SER,
  output Q,
  output QB
);

  wire and_1_out, and_2_out, and_3_out, and_4_out, and_5_out, and_6_out, and_7_out, and_8_out, and_9_out,
       and_10_out, and_11_out, and_12_out, and_13_out, and_14_out, and_15_out, and_16_out, and_17_out,
       d_ff_1_q, d_ff_2_q, d_ff_3_q, d_ff_4_q, d_ff_5_q, d_ff_6_q, d_ff_7_q, not_1_out, not_2_out, not_3_out,
       not_4_out, not_5_out, not_6_out, not_7_out, not_8_out, not_9_out, not_10_out;

  not not_1 (not_1_out, CLK_INH);
  not not_2 (not_2_out, SH_LDB);
  and and_1 (and_1_out, D0__7[0], not_2_out);
  and and_2 (and_2_out, not_1_out, CLK);
  not not_3 (not_3_out, and_1_out);
  and and_3 (and_3_out, D0__7[1], not_2_out);
  D_Flip_Flop d_ff_1 (
    .clk(and_2_out), .D(SER), .Q(d_ff_1_q), .preset(and_1_out), .en(1'b1), .reset(and_4_out));  // open: Qn
  and and_4 (and_4_out, not_3_out, not_2_out);
  not not_4 (not_4_out, and_3_out);
  and and_5 (and_5_out, D0__7[2], not_2_out);
  D_Flip_Flop d_ff_2 (
    .clk(and_2_out), .D(d_ff_1_q), .Q(d_ff_2_q), .preset(and_3_out), .en(1'b1), .reset(and_7_out));  // open: Qn
  and and_6 (and_6_out, not_5_out, not_2_out);
  and and_7 (and_7_out, not_4_out, not_2_out);
  not not_5 (not_5_out, and_5_out);
  and and_8 (and_8_out, D0__7[3], not_2_out);
  D_Flip_Flop d_ff_3 (
    .clk(and_2_out), .D(d_ff_2_q), .Q(d_ff_3_q), .preset(and_5_out), .en(1'b1), .reset(and_6_out));  // open: Qn
  D_Flip_Flop d_ff_4 (
    .clk(and_2_out), .D(d_ff_3_q), .Q(d_ff_4_q), .preset(and_8_out), .en(1'b1), .reset(and_9_out));  // open: Qn
  and and_9 (and_9_out, not_6_out, not_2_out);
  not not_6 (not_6_out, and_8_out);
  and and_10 (and_10_out, D0__7[5], not_2_out);
  and and_11 (and_11_out, D0__7[4], not_2_out);
  D_Flip_Flop d_ff_5 (
    .clk(and_2_out), .D(d_ff_4_q), .Q(d_ff_5_q), .preset(and_11_out), .en(1'b1), .reset(and_12_out));  // open: Qn
  and and_12 (and_12_out, not_7_out, not_2_out);
  not not_7 (not_7_out, and_11_out);
  and and_13 (and_13_out, D0__7[6], not_2_out);
  D_Flip_Flop d_ff_6 (
    .clk(and_2_out), .D(d_ff_5_q), .Q(d_ff_6_q), .preset(and_10_out), .en(1'b1), .reset(and_14_out));  // open: Qn
  and and_14 (and_14_out, not_8_out, not_2_out);
  not not_8 (not_8_out, and_10_out);
  and and_15 (and_15_out, D0__7[7], not_2_out);
  D_Flip_Flop d_ff_7 (
    .clk(and_2_out), .D(d_ff_6_q), .Q(d_ff_7_q), .preset(and_13_out), .en(1'b1), .reset(and_16_out));  // open: Qn
  and and_16 (and_16_out, not_9_out, not_2_out);
  not not_9 (not_9_out, and_13_out);
  D_Flip_Flop d_ff_8 (
    .clk(and_2_out), .D(d_ff_7_q), .Q(Q), .Qn(QB), .preset(and_15_out), .en(1'b1), .reset(and_17_out));
  and and_17 (and_17_out, not_10_out, not_2_out);
  not not_10 (not_10_out, and_15_out);
endmodule
